// Logisim project lap01.circ as structural Verilog: 1 circuit, main circuit main
module main (
  input  in_1,
  input  in_2,
  input  in_3,
  input  in_4,
  input  in_5,
  input  in_6,
  input  in_7,
  input  in_8,
  input  in_9,
  input  in_10,
  input  in_11,
  input  in_12,
  input  in_13,
  input  in_14,
  input  in_15,
  output out_16,
  output out_17,
  output out_18,
  output out_19,
  output out_20,
  output out_21,
  output out_22,
  output out_23,
  output out_24
);

  wire and_1_out, and_2_out, and_3_out, and_4_out, clock_1_out, clock_2_out, nand_1_out, nor_1_out,
       not_1_out, not_2_out, not_3_out, not_4_out, xnor_1_out;

  not not_1 (not_1_out, in_2);
  not not_2 (not_2_out, in_1);
  not not_3 (not_3_out, in_1);
  not not_4 (not_4_out, in_2);
  and and_1 (and_1_out, in_1, not_1_out);
  and and_2 (and_2_out, not_2_out, in_2);
  and and_3 (and_3_out, not_3_out, not_4_out);
  and and_4 (and_4_out, in_1, in_2);
  nor nor_1 (nor_1_out, in_7, in_8);
  nand nand_1 (nand_1_out, in_7, in_12);
  xnor xnor_1 (xnor_1_out, in_8, in_12);
  or or_1 (out_19, and_1_out, and_2_out);
  or or_2 (out_21, and_3_out, and_4_out);
  ExactlyOne xor_1 (.out(out_23), .in0(nor_1_out), .in1(nand_1_out), .in2(xnor_1_out));
  Clock clock_1 (.out(clock_1_out));
  Clock clock_2 (.out(clock_2_out));
  D_Flip_Flop d_ff_1 (.clk(clock_1_out), .D(in_9), .Q(out_22), .preset(in_10), .en(1'b1), .reset(in_11));  // open: Qn
  D_Flip_Flop d_ff_2 (.clk(clock_1_out), .D(in_13), .Q(out_24), .preset(in_14), .en(1'b1), .reset(in_15));  // open: Qn
  Register #(.width(4)) register_1 (
    .D({in_6, in_5, in_4, in_3}), .en(1'b1), .Q({out_20, out_18, out_17, out_16}), .clk(clock_2_out));  // open: clr
endmodule
