// Logisim project lap02.circ as structural Verilog: 1 circuit, main circuit main
module main (
  input  [1:0] in_1,
  input  [7:0] in_2,
  input  [7:0] in_3,
  input  [1:0] in_4,
  input  [7:0] in_5,
  input  in_6,
  output [7:0] out_7,
  output [7:0] out_8
);

  wire clock_1_out, decoder_1_out0, decoder_1_out2, decoder_1_out3;
  wire [7:0] adder_1_out, and_1_out, nand_1_out, register_1_q, register_2_q, register_3_q, register_4_q,
       subtractor_1_out;

  Adder adder_1 (.a(in_2), .b(in_3), .out(adder_1_out));  // open: cin, cout
  Subtractor subtractor_1 (.a(in_2), .b(in_3), .out(subtractor_1_out));  // open: bin, bout
  assign and_1_out = in_2 & in_3;  // AND_Gate and_1, 8 bits wide
  assign nand_1_out = ~(in_2 & in_3);  // NAND_Gate nand_1, 8 bits wide
  Multiplexer #(.select(2), .width(8)) multiplexer_1 (
    .in0(adder_1_out), .in1(subtractor_1_out), .in2(and_1_out), .in3(nand_1_out), .out(out_7), .sel(in_1));  // open: en
  Clock clock_1 (.out(clock_1_out));
  Decoder #(.select(2)) decoder_1 (
    .out0(decoder_1_out0), .out1(in_5[0]), .out2(decoder_1_out2), .out3(decoder_1_out3), .sel(in_4), .en(in_6));
  Register register_1 (.D(in_5), .en(decoder_1_out0), .Q(register_1_q), .clr(clock_1_out));  // open: clk
  Register register_2 (.D(in_5), .en(in_5[0]), .Q(register_2_q), .clr(in_5[0]));  // open: clk
  Register register_3 (.D(in_5), .en(decoder_1_out2), .Q(register_3_q), .clr(in_5[0]));  // open: clk
  Register register_4 (.D(in_5), .en(decoder_1_out3), .Q(register_4_q), .clr(clock_1_out));  // open: clk
  Multiplexer #(.select(2), .width(8)) multiplexer_2 (
    .in0(register_1_q), .in1(register_2_q), .in2(register_3_q), .in3(register_4_q), .out(out_8), .sel(in_4));  // open: en
  // Pins of 1 and 8 bits meet at in_5
endmodule
